# Fritzing sketch hc-sr04-sensor-circuit-diagram (saved by Fritzing 0.9.3b)
breadboards: 1

parts:
  WeMos_D1_Mini1 = WeMos D1 Mini
  R1 = Resistor [tolerance=±5% resistance=330 package=THT]
  R2 = Resistor [tolerance=±5% resistance=330 package=THT]
  Part1 = HC-SR04

nets:
  5V: WeMos_D1_Mini1.5V, Part1.Vcc
  N1: WeMos_D1_Mini1.D1, R1.Pin_1, R2.Pin_1
  N2: WeMos_D1_Mini1.D2, Part1.Trig
  N3: WeMos_D1_Mini1.G, R2.Pin_0, Part1.Gnd
  N4: R1.Pin_0, Part1.Echo

custom parts:
  HC-SR04: HC-SR04 ultrasonic distance sensor
